// Logisim project imm-gen.circ as structural Verilog: 1 circuit, main circuit imm_gen
module imm_gen (
  input  [31:0] Instruction,
  input  [2:0] ImmSel,
  output [31:0] Immediate
);

  wire [31:0] imm_CSRRWI, imm_I, imm_S, imm_SB, imm_UJ;

  assign imm_I = {{20{Instruction[31]}}, Instruction[31:20]};  // Bit_Extender bit_extender_1
  assign imm_S = {{20{Instruction[31]}}, {Instruction[31:25], Instruction[11:7]}};  // Bit_Extender bit_extender_2
  assign imm_SB = {{19{Instruction[31]}}, {Instruction[31], Instruction[7], Instruction[30:25], Instruction[11:8], 1'b0}};  // Bit_Extender bit_extender_3
  assign imm_UJ = {{11{Instruction[31]}}, {Instruction[31], Instruction[19:12], Instruction[20], Instruction[30:21], 1'b0}};  // Bit_Extender bit_extender_4
  assign imm_CSRRWI = {{27{1'b0}}, Instruction[19:15]};  // Bit_Extender bit_extender_5
  Multiplexer #(.select(3), .width(32)) multiplexer_1 (
    .in0(imm_I), .in1(imm_S), .in2(imm_SB), .in3({Instruction[31:12], {12{1'b0}}}), .in4(imm_UJ),
    .in5(imm_CSRRWI), .out(Immediate), .sel(ImmSel));  // open: in6, in7

  // Other names for the same wires on the sheet: inst[31:0] = Instruction; imm[31:0] = Immediate;
  //   imm_U[31:12] = Instruction[31:12]

  // Notes on the sheet:
  //   INPUTS to your circuit
  //   DON'T CHANGE THE LOCATIONS OF THE INPUTS AND OUTPUTS!
  //   OUTPUT from your circuit
endmodule
